// Logisim project TomasuloCadeirante.circ as structural Verilog: 14 circuits, main circuit main
module main (
  input  [1:0] in_1,
  input  [1:0] in_2,
  input  [1:0] in_3
);

  wire ALUSrc, and_1_out, and_3_out, and_4_out, and_5_out, and_6_out, and_7_out, and_8_out, Branch, Bsy_1,
       Bsy_2, Bsy_3, button_1_out, Clock1, clock_1_out, comparator_1_eq, comparator_2_eq, comparator_3_eq,
       comparator_4_eq, comparator_5_eq, comparator_6_eq, comparator_7_eq, comparator_8_eq, comparator_9_eq,
       comparator_10_eq, comparator_11_eq, demultiplexer_1_out0, Jump, MemtoReg, MemWrite, not_1_out,
       not_2_out, operandowriter_1_we_v_out, operandowriter_2_we_v_out, operandowriter_3_we_v_out,
       operandowriter_4_we_v_out, operandowriter_5_we_v_out, operandowriter_6_we_v_out, or_1_out, RegDst,
       RegWrite, set, uc_1_branch, uc_2_memtoreg, uc_2_memwrite, ULA2_Equal_Out, ula_1_equal, ula_2_equal,
       ULA_Equal_Out, WB_Dest_Enable, WB_Equal_Out, WE_1, WE_2, WE_3;
  wire [1:0] Read_Qi_1, Read_Qi_2, reservestation_1_q_1, reservestation_1_q_2, reservestation_2_q_1,
       reservestation_2_q_2, reservestation_3_q_1, reservestation_3_q_2, rs_selector_1_rs_selector_out,
       WB_RS_Out;
  wire [2:0] uc_ula_1_ulacode, uc_ula_2_ulacode;
  wire [4:0] DestReg, Reg_D_RS1, Reg_D_RS2, Reg_D_RS3, Shift_Amount, WB_Address_Out;
  wire [5:0] Funct, OpCode, reservestation_1_funct, reservestation_1_op, reservestation_2_funct,
       reservestation_2_op, reservestation_3_op;
  wire [9:0] adder_1_out, adder_2_out, multiplexer_1_out, multiplexer_2_out, register_1_q;
  wire [15:0] bit_extender_1_out, bit_extender_2_out, bit_extender_3_out, reservestation_1_a,
       reservestation_2_a, reservestation_3_a;
  wire [25:11] rom_1_data;
  wire [31:0] adder_3_out, bit_extender_4_out, bit_extender_5_out, Data_In, Data_Out, operandowriter_1_v_out,
       operandowriter_2_v_out, operandowriter_3_v_out, operandowriter_4_v_out, operandowriter_5_v_out,
       operandowriter_6_v_out, Read_Data_1, Read_Data_2, reservestation_1_v_1, reservestation_1_v_2,
       reservestation_2_v_1, reservestation_2_v_2, reservestation_3_v_1, reservestation_3_v_2, ULA2_Out,
       ula_1_ula_out, ula_2_ula_out, ULA_Out, WB_Data_Out;

  not not_1 (not_1_out, demultiplexer_1_out0);
  Register #(.width(10)) register_1 (
    .D(multiplexer_1_out), .en(set), .clk(and_1_out), .Q(register_1_q), .clr(button_1_out));
  and and_1 (and_1_out, Clock1, not_1_out);
  Button button_1 (.out(button_1_out));
  Multiplexer #(.width(10)) multiplexer_1 (
    .in0(multiplexer_2_out), .in1({Shift_Amount[3:0], Funct}), .out(multiplexer_1_out), .sel(Jump));
  ROM #(.addrWidth(10), .dataWidth(32)) rom_1 (.addr(register_1_q), .data({OpCode, rom_1_data, Shift_Amount, Funct}));
  Comparator #(.width(32)) comparator_1 (
    .a({OpCode, rom_1_data, Shift_Amount, Funct}), .b({32{1'b0}}), .eq(comparator_1_eq));  // open: gt, lt
  Clock clock_1 (.out(clock_1_out));
  Adder #(.width(10)) adder_1 (.a(10'h1), .b(register_1_q), .out(adder_1_out));  // open: cin, cout
  Adder #(.width(10)) adder_2 (.a(adder_1_out), .b({Shift_Amount[3:0], Funct}), .out(adder_2_out));  // open: cin, cout
  and NOP (Clock1, ~comparator_1_eq, clock_1_out);  // AND_Gate
  Multiplexer #(.width(10)) multiplexer_2 (.in0(adder_1_out), .in1(adder_2_out), .out(multiplexer_2_out), .sel(Branch));
  OperandoWriter operandowriter_1 (
    .Q(reservestation_1_q_1), .WB_RS(WB_RS_Out), .WE(WE_1), .V(Read_Data_1), .WB_Data(WB_Data_Out),
    .WE_V_Out(operandowriter_1_we_v_out), .V_Out(operandowriter_1_v_out));
  OperandoWriter operandowriter_2 (
    .Q(reservestation_1_q_2), .WB_RS(WB_RS_Out), .WE(WE_1), .V(Read_Data_2), .WB_Data(WB_Data_Out),
    .WE_V_Out(operandowriter_2_we_v_out), .V_Out(operandowriter_2_v_out));
  OperandoWriter operandowriter_3 (
    .Q(reservestation_2_q_1), .WB_RS(WB_RS_Out), .WE(WE_2), .V(Read_Data_1), .WB_Data(WB_Data_Out),
    .WE_V_Out(operandowriter_3_we_v_out), .V_Out(operandowriter_3_v_out));
  OperandoWriter operandowriter_4 (
    .Q(reservestation_2_q_2), .WB_RS(WB_RS_Out), .WE(WE_2), .V(Read_Data_2), .WB_Data(WB_Data_Out),
    .WE_V_Out(operandowriter_4_we_v_out), .V_Out(operandowriter_4_v_out));
  OperandoWriter operandowriter_5 (
    .Q(reservestation_3_q_1), .WB_RS(WB_RS_Out), .WE(WE_3), .V(Read_Data_1), .WB_Data(WB_Data_Out),
    .WE_V_Out(operandowriter_5_we_v_out), .V_Out(operandowriter_5_v_out));
  OperandoWriter operandowriter_6 (
    .Q(reservestation_3_q_2), .WB_RS(WB_RS_Out), .WE(WE_3), .V(Read_Data_2), .WB_Data(WB_Data_Out),
    .WE_V_Out(operandowriter_6_we_v_out), .V_Out(operandowriter_6_v_out));
  Comparator #(.width(2)) comparator_2 (.a(WB_RS_Out), .b(2'b01), .eq(comparator_2_eq));  // open: gt, lt
  Comparator #(.width(2)) comparator_3 (.a(WB_RS_Out), .b(2'b10), .eq(comparator_3_eq));  // open: gt, lt
  Comparator #(.width(2)) comparator_4 (.a(WB_RS_Out), .b(2'b11), .eq(comparator_4_eq));  // open: gt, lt
  assign bit_extender_1_out = {{11{Shift_Amount[4]}}, Shift_Amount};  // Bit_Extender bit_extender_1
  assign bit_extender_2_out = {{11{Shift_Amount[4]}}, Shift_Amount};  // Bit_Extender bit_extender_2
  assign bit_extender_3_out = {{11{Shift_Amount[4]}}, Shift_Amount};  // Bit_Extender bit_extender_3
  UC uc_1 (
    .OpCode(OpCode), .RegDst(RegDst), .Branch(uc_1_branch), .MemtoReg(MemtoReg), .MemWrite(MemWrite),
    .ALUSrc(ALUSrc), .RegWrite(RegWrite), .Jump(Jump));
  RS_Selector rs_selector_1 (
    .Bsy_1(Bsy_1), .Bsy_2(Bsy_2), .Bsy_3(Bsy_3), .Opcode(OpCode),
    .RS_Selector_Out(rs_selector_1_rs_selector_out));
  reserveStation reservestation_1 (
    .Clock(Clock1), .Bsy_in(1'b1), .Bsy_WE(WE_1), .Op_in(OpCode), .Op_WE(WE_1),
    .v1_in(operandowriter_1_v_out), .v1_WE(operandowriter_1_we_v_out), .v2_in(operandowriter_2_v_out),
    .v2_WE(operandowriter_2_we_v_out), .q1_in(Read_Qi_1), .q1_WE(WE_1), .q2_in(Read_Qi_2), .q2_WE(WE_1),
    .A_in(bit_extender_1_out), .A_WE(WE_1), .Reset(comparator_2_eq), .funct_in(Funct), .funct_WE(WE_1),
    .RegDest(DestReg), .RegDest_WE(WE_1), .Bsy(Bsy_1), .Op(reservestation_1_op), .v_1(reservestation_1_v_1),
    .v_2(reservestation_1_v_2), .q_1(reservestation_1_q_1), .q_2(reservestation_1_q_2),
    .A(reservestation_1_a), .funct(reservestation_1_funct), .Reg_D(Reg_D_RS1));
  reserveStation reservestation_2 (
    .Clock(Clock1), .Bsy_in(1'b1), .Bsy_WE(WE_2), .Op_in(OpCode), .Op_WE(WE_2),
    .v1_in(operandowriter_3_v_out), .v1_WE(operandowriter_3_we_v_out), .v2_in(operandowriter_4_v_out),
    .v2_WE(operandowriter_4_we_v_out), .q1_in(Read_Qi_1), .q1_WE(WE_2), .q2_in(Read_Qi_2), .q2_WE(WE_2),
    .A_in(bit_extender_2_out), .A_WE(WE_2), .Reset(comparator_3_eq), .funct_in(Funct), .funct_WE(WE_2),
    .RegDest(DestReg), .RegDest_WE(WE_2), .Bsy(Bsy_2), .Op(reservestation_2_op), .v_1(reservestation_2_v_1),
    .v_2(reservestation_2_v_2), .q_1(reservestation_2_q_1), .q_2(reservestation_2_q_2),
    .A(reservestation_2_a), .funct(reservestation_2_funct), .Reg_D(Reg_D_RS2));
  reserveStation reservestation_3 (
    .Clock(Clock1), .Bsy_in(1'b1), .Bsy_WE(WE_2), .Op_in(OpCode), .Op_WE(WE_2),
    .v1_in(operandowriter_5_v_out), .v1_WE(operandowriter_5_we_v_out), .v2_in(operandowriter_6_v_out),
    .v2_WE(operandowriter_6_we_v_out), .q1_in(Read_Qi_1), .q1_WE(WE_2), .q2_in(Read_Qi_2), .q2_WE(WE_2),
    .A_in(bit_extender_3_out), .A_WE(WE_2), .Reset(comparator_4_eq), .funct_in(Funct), .funct_WE(WE_2),
    .RegDest(DestReg), .RegDest_WE(WE_2), .Bsy(Bsy_3), .Op(reservestation_3_op), .v_1(reservestation_3_v_1),
    .v_2(reservestation_3_v_2), .q_1(reservestation_3_q_1), .q_2(reservestation_3_q_2),
    .A(reservestation_3_a), .Reg_D(Reg_D_RS3));  // open: funct
  Demultiplexer #(.select(2)) demultiplexer_1 (
    .out0(demultiplexer_1_out0), .out1(WE_1), .out2(WE_2), .out3(WE_3), .in(1'b1),
    .sel(rs_selector_1_rs_selector_out));
  Comparator #(.width(2)) comparator_5 (
    .a(rs_selector_1_rs_selector_out), .b(2'b00), .eq(comparator_5_eq));  // open: gt, lt
  and and_2 (Branch, uc_1_branch, WB_Dest_Enable);
  Multiplexer #(.width(5)) multiplexer_3 (
    .in0(rom_1_data[15:11]), .in1(rom_1_data[20:16]), .out(DestReg), .sel(RegDst));
  not not_2 (not_2_out, comparator_5_eq);
  Comparator #(.width(2)) comparator_6 (.a(reservestation_1_q_1), .b(in_1), .eq(comparator_6_eq));  // open: gt, lt
  Comparator #(.width(2)) comparator_7 (.a(reservestation_1_q_2), .b(in_1), .eq(comparator_7_eq));  // open: gt, lt
  Comparator #(.width(2)) comparator_8 (.a(reservestation_3_q_1), .b(in_3), .eq(comparator_8_eq));  // open: gt, lt
  Comparator #(.width(2)) comparator_9 (.a(reservestation_3_q_2), .b(in_3), .eq(comparator_9_eq));  // open: gt, lt
  Comparator #(.width(2)) comparator_10 (.a(reservestation_2_q_1), .b(in_2), .eq(comparator_10_eq));  // open: gt, lt
  Comparator #(.width(2)) comparator_11 (.a(reservestation_2_q_2), .b(in_2), .eq(comparator_11_eq));  // open: gt, lt
  UC uc_2 (
    .OpCode(reservestation_3_op), .MemtoReg(uc_2_memtoreg), .MemWrite(uc_2_memwrite));  // open: RegDst, Branch, ALUSrc, RegWrite, Jump
  assign bit_extender_4_out = {{16{rom_1_data[15]}}, {rom_1_data[15:11], Shift_Amount, Funct}};  // Bit_Extender bit_extender_4
  and and_3 (and_3_out, comparator_6_eq, comparator_7_eq);
  UC_ula uc_ula_1 (.funct(reservestation_1_funct), .OpCode(reservestation_1_op), .ULAcode(uc_ula_1_ulacode));
  and and_4 (and_4_out, comparator_10_eq, comparator_11_eq);
  and and_5 (and_5_out, comparator_8_eq, comparator_9_eq);
  UC_ula uc_ula_2 (.funct(reservestation_2_funct), .OpCode(reservestation_2_op), .ULAcode(uc_ula_2_ulacode));
  assign bit_extender_5_out = {{16{reservestation_3_a[15]}}, reservestation_3_a};  // Bit_Extender bit_extender_5
  and and_6 (and_6_out, and_3_out, Clock1);
  and and_7 (and_7_out, and_4_out, Clock1);
  and and_8 (and_8_out, and_5_out, Clock1);
  Adder #(.width(32)) adder_3 (.a(reservestation_3_v_2), .b(bit_extender_5_out), .out(adder_3_out));  // open: cin, cout
  RegBank regbank_1 (
    .Addr_Register1(rom_1_data[25:21]), .Addr_Register2(rom_1_data[20:16]), .Write_Data(WB_Data_Out),
    .RegWE(WB_Dest_Enable), .Write_Reg(WB_Address_Out), .WB_RS(WB_RS_Out),
    .Qi_in(rs_selector_1_rs_selector_out), .QiWriteEnable(not_2_out), .Reg_Dest_Qi(DestReg), .Clock(Clock1),
    .Read_Data_1(Read_Data_1), .Read_Data_2(Data_In), .Read_Qi_1(Read_Qi_1), .Read_Qi_2(Read_Qi_2));
  ULA ula_1 (
    .A(reservestation_1_v_1), .B(reservestation_1_v_2), .Op(uc_ula_1_ulacode),
    .shamt(reservestation_1_a[4:0]), .ULA_out(ula_1_ula_out), .Equal(ula_1_equal));
  Multiplexer #(.width(32)) multiplexer_4 (.in0(Data_In), .in1(bit_extender_4_out), .out(Read_Data_2), .sel(ALUSrc));
  Register #(.width(32)) register_2 (.D(ula_1_ula_out), .en(and_6_out), .clk(and_6_out), .Q(ULA_Out));  // open: clr
  Register #(.width(1)) register_3 (.D(ula_1_equal), .en(and_6_out), .clk(and_6_out), .Q(ULA_Equal_Out));  // open: clr
  Register #(.width(32)) register_4 (.D(ula_2_ula_out), .en(and_7_out), .clk(and_7_out), .Q(ULA2_Out));  // open: clr
  ULA ula_2 (
    .A(reservestation_2_v_1), .B(reservestation_2_v_2), .Op(uc_ula_2_ulacode),
    .shamt(reservestation_2_a[4:0]), .ULA_out(ula_2_ula_out), .Equal(ula_2_equal));
  Register #(.width(1)) register_5 (.D(ula_2_equal), .en(and_7_out), .clk(and_7_out), .Q(ULA2_Equal_Out));  // open: clr
  memoria memoria_1 (
    .in_1(and_8_out), .Data_In(reservestation_3_v_1), .ReadEnable(uc_2_memtoreg),
    .WriteEnable(uc_2_memwrite), .Address(adder_3_out[21:2]), .DataOut(Data_Out));  // open: Stall
  or or_1 (or_1_out, Bsy_1, Bsy_2, Bsy_3);
  WriteBack writeback_1 (
    .Result_Data1(ULA_Out), .Fin_RS_1(Bsy_1), .Result_Data2(ULA2_Out), .Fin_RS_2(Bsy_2),
    .Result_Data3(Data_Out), .Fin_RS_3(Bsy_3), .Write_Enable(or_1_out), .Clock(Clock1),
    .Reg_D_RS1(Reg_D_RS1), .Reg_D_RS2(Reg_D_RS2), .Reg_D_RS3(Reg_D_RS3), .Equal_RS1(ULA_Equal_Out),
    .Equal_RS2(ULA2_Equal_Out), .WB_Data_Out(WB_Data_Out), .WB_Address_Out(WB_Address_Out),
    .WB_Equal_Out(WB_Equal_Out), .WB_Dest_Enable(WB_Dest_Enable), .WB_RS_Out(WB_RS_Out));  // open: Equal_RS3

  // Notes on the sheet:
  //   contents of rom_1 (hex, n*v repeats v):
  //   24080000 24090000 240a0005 240d000a 112d0005 96080 10c5820 8d700000 25290001 8100004
  //   Unidade Funcional ULA 1
  //   Unidade Funcional ULA 2
  //   Unidade Funcional Mémoria (3)
endmodule

module RegisterFile (
  input  [4:0] Read_Register_1,
  input  [4:0] Read_Register_2,
  input  [31:0] Write_Data,
  input  RegWrite,
  input  [4:0] Write_Register,
  input  Clock,
  output [31:0] Read_Data_1,
  output [31:0] Read_Data_2
);

  wire demultiplexer_1_out0, demultiplexer_1_out1, demultiplexer_1_out2, demultiplexer_1_out3,
       demultiplexer_1_out4, demultiplexer_1_out5, demultiplexer_1_out6, demultiplexer_1_out7,
       demultiplexer_1_out8, demultiplexer_1_out9, demultiplexer_1_out10, demultiplexer_1_out11,
       demultiplexer_1_out12, demultiplexer_1_out13, demultiplexer_1_out14, demultiplexer_1_out15,
       demultiplexer_1_out16, demultiplexer_1_out17, demultiplexer_1_out18, demultiplexer_1_out19,
       demultiplexer_1_out20, demultiplexer_1_out21, demultiplexer_1_out22, demultiplexer_1_out23,
       demultiplexer_1_out24, demultiplexer_1_out25, demultiplexer_1_out26, demultiplexer_1_out27,
       demultiplexer_1_out28, demultiplexer_1_out29, demultiplexer_1_out30, demultiplexer_1_out31;
  wire [31:0] register_1_q, register_2_q, register_3_q, register_4_q, register_5_q, register_6_q,
       register_7_q, register_8_q, register_9_q, register_10_q, register_11_q, register_12_q, register_13_q,
       register_14_q, register_15_q, register_16_q, register_17_q, register_18_q, register_19_q,
       register_20_q, register_21_q, register_22_q, register_23_q, register_24_q, register_25_q,
       register_26_q, register_27_q, register_28_q, register_29_q, register_30_q, register_31_q,
       register_32_q;

  Demultiplexer #(.enable("true"), .select(5)) demultiplexer_1 (
    .out0(demultiplexer_1_out0), .out1(demultiplexer_1_out1), .out2(demultiplexer_1_out2),
    .out3(demultiplexer_1_out3), .out4(demultiplexer_1_out4), .out5(demultiplexer_1_out5),
    .out6(demultiplexer_1_out6), .out7(demultiplexer_1_out7), .out8(demultiplexer_1_out8),
    .out9(demultiplexer_1_out9), .out10(demultiplexer_1_out10), .out11(demultiplexer_1_out11),
    .out12(demultiplexer_1_out12), .out13(demultiplexer_1_out13), .out14(demultiplexer_1_out14),
    .out15(demultiplexer_1_out15), .out16(demultiplexer_1_out16), .out17(demultiplexer_1_out17),
    .out18(demultiplexer_1_out18), .out19(demultiplexer_1_out19), .out20(demultiplexer_1_out20),
    .out21(demultiplexer_1_out21), .out22(demultiplexer_1_out22), .out23(demultiplexer_1_out23),
    .out24(demultiplexer_1_out24), .out25(demultiplexer_1_out25), .out26(demultiplexer_1_out26),
    .out27(demultiplexer_1_out27), .out28(demultiplexer_1_out28), .out29(demultiplexer_1_out29),
    .out30(demultiplexer_1_out30), .out31(demultiplexer_1_out31), .in(RegWrite), .sel(Write_Register));  // open: en
  Register #(.width(32)) register_1 (
    .D(Write_Data), .en(demultiplexer_1_out1), .Q(register_1_q), .clk(Clock));  // open: clr
  Register #(.width(32)) register_2 (
    .D(Write_Data), .en(demultiplexer_1_out0), .Q(register_2_q), .clk(Clock));  // open: clr
  Register #(.width(32)) register_3 (
    .D(Write_Data), .en(demultiplexer_1_out9), .Q(register_3_q), .clk(Clock));  // open: clr
  Register #(.width(32)) register_4 (
    .D(Write_Data), .en(demultiplexer_1_out8), .Q(register_4_q), .clk(Clock));  // open: clr
  Register #(.width(32)) register_5 (
    .D(Write_Data), .en(demultiplexer_1_out17), .Q(register_5_q), .clk(Clock));  // open: clr
  Register #(.width(32)) register_6 (
    .D(Write_Data), .en(demultiplexer_1_out16), .Q(register_6_q), .clk(Clock));  // open: clr
  Register #(.width(32)) register_7 (
    .D(Write_Data), .en(demultiplexer_1_out25), .Q(register_7_q), .clk(Clock));  // open: clr
  Register #(.width(32)) register_8 (
    .D(Write_Data), .en(demultiplexer_1_out24), .Q(register_8_q), .clk(Clock));  // open: clr
  Register #(.width(32)) register_9 (
    .D(Write_Data), .en(demultiplexer_1_out2), .Q(register_9_q), .clk(Clock));  // open: clr
  Register #(.width(32)) register_10 (
    .D(Write_Data), .en(demultiplexer_1_out10), .Q(register_10_q), .clk(Clock));  // open: clr
  Register #(.width(32)) register_11 (
    .D(Write_Data), .en(demultiplexer_1_out18), .Q(register_11_q), .clk(Clock));  // open: clr
  Register #(.width(32)) register_12 (
    .D(Write_Data), .en(demultiplexer_1_out26), .Q(register_12_q), .clk(Clock));  // open: clr
  Register #(.width(32)) register_13 (
    .D(Write_Data), .en(demultiplexer_1_out3), .Q(register_13_q), .clk(Clock));  // open: clr
  Register #(.width(32)) register_14 (
    .D(Write_Data), .en(demultiplexer_1_out11), .Q(register_14_q), .clk(Clock));  // open: clr
  Register #(.width(32)) register_15 (
    .D(Write_Data), .en(demultiplexer_1_out19), .Q(register_15_q), .clk(Clock));  // open: clr
  Register #(.width(32)) register_16 (
    .D(Write_Data), .en(demultiplexer_1_out27), .Q(register_16_q), .clk(Clock));  // open: clr
  Register #(.width(32)) register_17 (
    .D(Write_Data), .en(demultiplexer_1_out4), .Q(register_17_q), .clk(Clock));  // open: clr
  Register #(.width(32)) register_18 (
    .D(Write_Data), .en(demultiplexer_1_out12), .Q(register_18_q), .clk(Clock));  // open: clr
  Register #(.width(32)) register_19 (
    .D(Write_Data), .en(demultiplexer_1_out20), .Q(register_19_q), .clk(Clock));  // open: clr
  Register #(.width(32)) register_20 (
    .D(Write_Data), .en(demultiplexer_1_out28), .Q(register_20_q), .clk(Clock));  // open: clr
  Register #(.width(32)) register_21 (
    .D(Write_Data), .en(demultiplexer_1_out5), .Q(register_21_q), .clk(Clock));  // open: clr
  Register #(.width(32)) register_22 (
    .D(Write_Data), .en(demultiplexer_1_out13), .Q(register_22_q), .clk(Clock));  // open: clr
  Register #(.width(32)) register_23 (
    .D(Write_Data), .en(demultiplexer_1_out21), .Q(register_23_q), .clk(Clock));  // open: clr
  Register #(.width(32)) register_24 (
    .D(Write_Data), .en(demultiplexer_1_out29), .Q(register_24_q), .clk(Clock));  // open: clr
  Register #(.width(32)) register_25 (
    .D(Write_Data), .en(demultiplexer_1_out6), .Q(register_25_q), .clk(Clock));  // open: clr
  Register #(.width(32)) register_26 (
    .D(Write_Data), .en(demultiplexer_1_out14), .Q(register_26_q), .clk(Clock));  // open: clr
  Register #(.width(32)) register_27 (
    .D(Write_Data), .en(demultiplexer_1_out22), .Q(register_27_q), .clk(Clock));  // open: clr
  Register #(.width(32)) register_28 (
    .D(Write_Data), .en(demultiplexer_1_out30), .Q(register_28_q), .clk(Clock));  // open: clr
  Register #(.width(32)) register_29 (
    .D(Write_Data), .en(demultiplexer_1_out7), .Q(register_29_q), .clk(Clock));  // open: clr
  Register #(.width(32)) register_30 (
    .D(Write_Data), .en(demultiplexer_1_out15), .Q(register_30_q), .clk(Clock));  // open: clr
  Register #(.width(32)) register_31 (
    .D(Write_Data), .en(demultiplexer_1_out23), .Q(register_31_q), .clk(Clock));  // open: clr
  Register #(.width(32)) register_32 (
    .D(Write_Data), .en(demultiplexer_1_out31), .Q(register_32_q), .clk(Clock));  // open: clr
  Multiplexer #(.enable("true"), .select(5), .width(32)) multiplexer_1 (
    .in0({32{1'b0}}), .in1(register_1_q), .in2(register_9_q), .in3(register_13_q), .in4(register_17_q),
    .in5(register_21_q), .in6(register_25_q), .in7(register_29_q), .in8(register_4_q), .in9(register_3_q),
    .in10(register_10_q), .in11(register_14_q), .in12(register_18_q), .in13(register_22_q),
    .in14(register_26_q), .in15(register_30_q), .in16(register_6_q), .in17(register_5_q),
    .in18(register_11_q), .in19(register_15_q), .in20(register_19_q), .in21(register_23_q),
    .in22(register_27_q), .in23(register_31_q), .in24(register_8_q), .in25(register_7_q),
    .in26(register_12_q), .in27(register_16_q), .in28(register_20_q), .in29(register_24_q),
    .in30(register_28_q), .in31(register_32_q), .out(Read_Data_1), .sel(Read_Register_1));  // open: en
  Multiplexer #(.enable("true"), .select(5), .width(32)) multiplexer_2 (
    .in0({32{1'b0}}), .in1(register_1_q), .in2(register_9_q), .in3(register_13_q), .in4(register_17_q),
    .in5(register_21_q), .in6(register_25_q), .in7(register_29_q), .in8(register_4_q), .in9(register_3_q),
    .in10(register_10_q), .in11(register_14_q), .in12(register_18_q), .in13(register_22_q),
    .in14(register_26_q), .in15(register_30_q), .in16(register_6_q), .in17(register_5_q),
    .in18(register_11_q), .in19(register_15_q), .in20(register_19_q), .in21(register_23_q),
    .in22(register_27_q), .in23(register_31_q), .in24(register_8_q), .in25(register_7_q),
    .in26(register_12_q), .in27(register_16_q), .in28(register_20_q), .in29(register_24_q),
    .in30(register_28_q), .in31(register_32_q), .out(Read_Data_2), .sel(Read_Register_2));  // open: en
endmodule

module ULA (
  input  [31:0] A,
  input  [31:0] B,
  input  [2:0] Op,
  input  [4:0] shamt,
  output [31:0] ULA_out,
  output Equal
);

  wire comparator_1_lt;
  wire [31:0] adder_1_out, multiplexer_1_out, nor_1_out, shifter_1_out, subtractor_1_out;

  Adder #(.width(32)) adder_1 (.a(A), .b(B), .out(adder_1_out));  // open: cin, cout
  Subtractor #(.width(32)) subtractor_1 (.a(A), .b(B), .out(subtractor_1_out));  // open: bin, bout
  assign nor_1_out = ~(A | B);  // NOR_Gate nor_1, 32 bits wide
  Comparator #(.width(32)) comparator_1 (.a(A), .b(B), .eq(Equal), .lt(comparator_1_lt));  // open: gt
  Multiplexer #(.width(32)) multiplexer_1 (
    .in0({32{1'b0}}), .in1(32'h1), .out(multiplexer_1_out), .sel(comparator_1_lt));
  Shifter #(.width(32)) shifter_1 (.in(B), .\dist (shamt), .out(shifter_1_out));
  Multiplexer #(.select(3), .width(32)) multiplexer_2 (
    .in0(subtractor_1_out), .in1(nor_1_out), .in2(multiplexer_1_out), .in3(shifter_1_out), .in4(adder_1_out),
    .in5(adder_1_out), .in6(adder_1_out), .in7(adder_1_out), .out(ULA_out), .sel(Op));
endmodule

module UC (
  input  [5:0] OpCode,
  output RegDst,
  output Branch,
  output MemtoReg,
  output MemWrite,
  output ALUSrc,
  output RegWrite,
  output Jump
);

  wire ADDIU_out, Tipo_R_out;

  and J (Jump, ~OpCode[5], ~OpCode[4], ~OpCode[3], ~OpCode[2], OpCode[1], ~OpCode[0]);  // AND_Gate
  and BEQ (Branch, ~OpCode[5], ~OpCode[4], ~OpCode[3], OpCode[2], ~OpCode[1], ~OpCode[0]);  // AND_Gate
  and SW (MemWrite, OpCode[5], ~OpCode[4], OpCode[3], ~OpCode[2], OpCode[1], OpCode[0]);  // AND_Gate
  and LW (MemtoReg, OpCode[5], ~OpCode[4], ~OpCode[3], ~OpCode[2], OpCode[1], OpCode[0]);  // AND_Gate
  and ADDIU (ADDIU_out, ~OpCode[5], ~OpCode[4], OpCode[3], ~OpCode[2], ~OpCode[1], OpCode[0]);  // AND_Gate
  and Tipo_R (Tipo_R_out, ~OpCode[5], ~OpCode[4], ~OpCode[3], ~OpCode[2], ~OpCode[1], ~OpCode[0]);  // AND_Gate
  or or_1 (RegDst, ADDIU_out, MemtoReg);
  or or_2 (ALUSrc, ADDIU_out, MemtoReg, MemWrite);
  or or_3 (RegWrite, Tipo_R_out, ADDIU_out, MemtoReg);
endmodule

module UC_ula (
  input  [5:0] funct,
  input  [5:0] OpCode,
  output [2:0] ULAcode
);

  wire NOR0_out, nor_1_out, not_R_out, SLL0_out, SLT0_out, SUB0_out;

  and SLL0 (SLL0_out, ~funct[5], ~funct[4], ~funct[3], ~funct[2], ~funct[1], ~funct[0]);  // AND_Gate
  and SLT0 (SLT0_out, funct[5], ~funct[4], funct[3], ~funct[2], funct[1], ~funct[0]);  // AND_Gate
  and NOR0 (NOR0_out, funct[5], ~funct[4], ~funct[3], funct[2], funct[1], funct[0]);  // AND_Gate
  nand not_R (not_R_out, ~OpCode[0], ~OpCode[1], ~OpCode[2], ~OpCode[3], ~OpCode[4], ~OpCode[5]);  // NAND_Gate
  and SUB0 (SUB0_out, funct[5], ~funct[4], ~funct[3], ~funct[2], funct[1], ~funct[0]);  // AND_Gate
  or or_1 (ULAcode[0], NOR0_out, SLL0_out);
  or or_2 (ULAcode[1], SLT0_out, SLL0_out);
  nor nor_1 (nor_1_out, SUB0_out, NOR0_out, SLT0_out, SLL0_out);
  or or_3 (ULAcode[2], nor_1_out, not_R_out);
endmodule

module memoria (
  input  in_1,
  input  [31:0] Data_In,
  input  ReadEnable,
  input  WriteEnable,
  input  [19:0] Address,
  output Stall,
  output [31:0] DataOut
);

  wire and_1_out, and_2_out, and_3_out, and_4_out, cache_1_hit, ClockofRAM, demultiplexer_1_out0,
       demultiplexer_1_out1, demultiplexer_1_out2, demultiplexer_1_out3, Miss, not_1_out, not_2_out,
       or_1_out, register_1_q, S1, S2, t_ff_1_q;
  wire [31:0] ram_1_dout, ram_2_dout, ram_3_dout, ram_4_dout;

  clockRAM clockram_1 (.ClockIN(in_1), .ClockOut(ClockofRAM));
  Demultiplexer #(.select(2)) demultiplexer_1 (
    .out0(demultiplexer_1_out0), .out1(demultiplexer_1_out1), .out2(demultiplexer_1_out2),
    .out3(demultiplexer_1_out3), .in(WriteEnable), .sel(Address[1:0]));
  RAM #(.addrWidth(18), .dataWidth(32), .enables("line")) ram_1 (
    .addr(Address[19:2]), .we(demultiplexer_1_out0), .clk(ClockofRAM), .din(Data_In), .dout(ram_1_dout));
  RAM #(.addrWidth(18), .dataWidth(32), .enables("line")) ram_2 (
    .addr(Address[19:2]), .we(demultiplexer_1_out1), .clk(ClockofRAM), .din(Data_In), .dout(ram_2_dout));
  RAM #(.addrWidth(18), .dataWidth(32), .enables("line")) ram_3 (
    .addr(Address[19:2]), .we(demultiplexer_1_out2), .clk(ClockofRAM), .din(Data_In), .dout(ram_3_dout));
  RAM #(.addrWidth(18), .dataWidth(32), .enables("line")) ram_4 (
    .addr(Address[19:2]), .we(demultiplexer_1_out3), .clk(ClockofRAM), .din(Data_In), .dout(ram_4_dout));
  and and_1 (and_1_out, ReadEnable, Miss);
  or or_1 (or_1_out, WriteEnable, and_1_out);
  not not_1 (not_1_out, S2);
  not not_2 (not_2_out, S1);
  T_Flip_Flop t_ff_1 (.T(or_1_out), .clk(in_1), .Q(t_ff_1_q), .reset(register_1_q));  // open: Qn, preset
  and and_2 (and_2_out, WriteEnable, not_1_out);
  and and_3 (and_3_out, and_1_out, not_2_out);
  and and_4 (and_4_out, WriteEnable, t_ff_1_q);
  T_Flip_Flop t_ff_2 (.T(and_4_out), .clk(in_1), .Q(S1), .reset(register_1_q));  // open: Qn, preset
  and and_5 (S2, t_ff_1_q, S1);
  Register #(.width(1)) register_1 (.D(S2), .en(in_1), .clk(in_1), .Q(register_1_q));  // open: clr
  or or_2 (Stall, and_2_out, and_3_out);
  not not_3 (Miss, cache_1_hit);
  Cache cache_1 (
    .MemIn1(ram_1_dout), .MemIn2(ram_2_dout), .MemIn3(ram_3_dout), .MemIn4(ram_4_dout), .Clock(in_1),
    .ReadEnable(ReadEnable), .WriteEnable(WriteEnable), .Address(Address), .Hit(cache_1_hit),
    .DataOut(DataOut));

  // Other names for the same wires on the sheet: AdrMem[17:0] = Address[19:2]; Clock = in_1; RE = ReadEnable;
  //   WE = WriteEnable
endmodule

module clockRAM (
  input  ClockIN,
  output ClockOut
);

  wire button_1_out;

  Button button_1 (.out(button_1_out));
  T_Flip_Flop t_ff_1 (.T(ClockIN), .clk(ClockIN), .Q(ClockOut), .reset(button_1_out));  // open: Qn, preset
endmodule

module Cache (
  input  [31:0] MemIn1,
  input  [31:0] MemIn2,
  input  [31:0] MemIn3,
  input  [31:0] MemIn4,
  input  Clock,
  input  ReadEnable,
  input  WriteEnable,
  input  [19:0] Address,
  output Hit,
  output [31:0] DataOut
);

  wire and_1_out, and_2_out, comparator_1_eq, d_ff_1_q, not_1_out, register_3_q, t_ff_1_q, t_ff_2_q, WE;
  wire [15:0] bit_extender_1_out, register_1_q, register_2_q, tag_dout;
  wire [31:0] Out1, Out2, Out3, Out4;

  not not_1 (not_1_out, Hit);
  D_Flip_Flop d_ff_1 (.D(not_1_out), .clk(Clock), .Q(d_ff_1_q));  // open: Qn, preset, reset
  or or_1 (WE, d_ff_1_q, WriteEnable);
  RAM #(.addrWidth(3), .dataWidth(32)) RAMCache1 (
    .addr(Address[4:2]), .we(WE), .oe(ReadEnable), .clk(Clock), .din(MemIn1), .dout(Out1));
  assign bit_extender_1_out = {{1{1'b1}}, Address[19:5]};  // Bit_Extender bit_extender_1
  Register #(.width(16)) register_1 (.D(bit_extender_1_out), .en(WE), .clk(Clock), .Q(register_1_q), .clr(and_2_out));
  T_Flip_Flop t_ff_1 (.T(WE), .clk(Clock), .Q(t_ff_1_q), .reset(and_2_out));  // open: Qn, preset
  Register #(.width(16)) register_2 (.D(register_1_q), .en(WE), .clk(t_ff_1_q), .Q(register_2_q), .clr(and_2_out));
  T_Flip_Flop t_ff_2 (.T(t_ff_1_q), .clk(Clock), .Q(t_ff_2_q), .reset(and_2_out));  // open: Qn, preset
  Register #(.width(1)) register_3 (.D(and_1_out), .en(Clock), .clk(Clock), .Q(register_3_q), .clr(and_2_out));
  and and_1 (and_1_out, t_ff_1_q, t_ff_2_q);
  RAM #(.addrWidth(3), .dataWidth(32)) RAMCache2 (
    .addr(Address[4:2]), .we(WE), .oe(ReadEnable), .clk(Clock), .din(MemIn2), .dout(Out2));
  and and_2 (and_2_out, register_3_q, t_ff_1_q);
  RAM #(.addrWidth(3), .dataWidth(16), .enables("line")) tag (
    .addr(Address[4:2]), .we(WE), .clk(Clock), .din(register_2_q), .dout(tag_dout));
  RAM #(.addrWidth(3), .dataWidth(32)) RAMCache3 (
    .addr(Address[4:2]), .we(WE), .oe(ReadEnable), .clk(Clock), .din(MemIn3), .dout(Out3));
  Comparator #(.width(15)) comparator_1 (.a(Address[19:5]), .b(tag_dout[14:0]), .eq(comparator_1_eq));  // open: gt, lt
  and and_3 (Hit, comparator_1_eq, tag_dout[15]);
  Multiplexer #(.select(2), .width(32)) multiplexer_1 (
    .in0(Out1), .in1(Out2), .in2(Out3), .in3(Out4), .out(DataOut), .sel(Address[1:0]));
  RAM #(.addrWidth(3), .dataWidth(32)) RAMCache4 (
    .addr(Address[4:2]), .we(WE), .oe(ReadEnable), .clk(Clock), .din(MemIn4), .dout(Out4));

  // Other names for the same wires on the sheet: Ad[19:0] = Address; Offset[1:0] = Address[1:0];
  //   Line[2:0] = Address[4:2]; Tag[14:0] = Address[19:5]; MI1[31:0] = MemIn1; MI2[31:0] = MemIn2; MI3[31:0] = MemIn3;
  //   MI4[31:0] = MemIn4; RE = ReadEnable
endmodule

module RegBank (
  input  [4:0] Addr_Register1,
  input  [4:0] Addr_Register2,
  input  [31:0] Write_Data,
  input  RegWE,
  input  [4:0] Write_Reg,
  input  [1:0] WB_RS,
  input  [1:0] Qi_in,
  input  QiWriteEnable,
  input  [4:0] Reg_Dest_Qi,
  input  Clock,
  output [31:0] Read_Data_1,
  output [31:0] Read_Data_2,
  output [1:0] Read_Qi_1,
  output [1:0] Read_Qi_2
);

  wire and_1_out, comparator_1_eq, comparator_2_eq, comparator_3_eq;
  wire [1:0] qibank_1_read_data_3;
  wire [4:0] multiplexer_1_out, multiplexer_2_out;

  QiBank qibank_1 (
    .Read_Register_1(Addr_Register1), .Read_Register_2(Addr_Register2), .Read_Register_3(Write_Reg),
    .Write_Data(Qi_in), .RegWrite(QiWriteEnable), .Write_Register(Reg_Dest_Qi), .Clock(Clock),
    .Read_Data_1(Read_Qi_1), .Read_Data_2(Read_Qi_2), .Read_Data_3(qibank_1_read_data_3));
  Comparator #(.mode("unsigned"), .width(2)) comparator_1 (
    .a(WB_RS), .b(qibank_1_read_data_3), .eq(comparator_1_eq));  // open: gt, lt
  and and_1 (and_1_out, RegWE, comparator_1_eq);
  Comparator #(.mode("unsigned"), .width(2)) comparator_2 (
    .a(Read_Qi_1), .b(2'b00), .eq(comparator_2_eq));  // open: gt, lt
  Comparator #(.mode("unsigned"), .width(2)) comparator_3 (
    .a(2'b00), .b(Read_Qi_2), .eq(comparator_3_eq));  // open: gt, lt
  Multiplexer #(.width(5)) multiplexer_1 (
    .in0({5{1'b0}}), .in1(Addr_Register1), .out(multiplexer_1_out), .sel(comparator_2_eq));
  Multiplexer #(.width(5)) multiplexer_2 (
    .in0({5{1'b0}}), .in1(Addr_Register2), .out(multiplexer_2_out), .sel(comparator_3_eq));
  RegisterFile registerfile_1 (
    .Read_Register_1(multiplexer_1_out), .Read_Register_2(multiplexer_2_out), .Write_Data(Write_Data),
    .RegWrite(and_1_out), .Write_Register(Write_Reg), .Clock(Clock), .Read_Data_1(Read_Data_1),
    .Read_Data_2(Read_Data_2));
endmodule

module QiBank (
  input  [4:0] Read_Register_1,
  input  [4:0] Read_Register_2,
  input  [4:0] Read_Register_3,
  input  [1:0] Write_Data,
  input  RegWrite,
  input  [4:0] Write_Register,
  input  Clock,
  output [1:0] Read_Data_1,
  output [1:0] Read_Data_2,
  output [1:0] Read_Data_3
);

  wire demultiplexer_1_out0, demultiplexer_1_out1, demultiplexer_1_out2, demultiplexer_1_out3,
       demultiplexer_1_out4, demultiplexer_1_out5, demultiplexer_1_out6, demultiplexer_1_out7,
       demultiplexer_1_out8, demultiplexer_1_out9, demultiplexer_1_out10, demultiplexer_1_out11,
       demultiplexer_1_out12, demultiplexer_1_out13, demultiplexer_1_out14, demultiplexer_1_out15,
       demultiplexer_1_out16, demultiplexer_1_out17, demultiplexer_1_out18, demultiplexer_1_out19,
       demultiplexer_1_out20, demultiplexer_1_out21, demultiplexer_1_out22, demultiplexer_1_out23,
       demultiplexer_1_out24, demultiplexer_1_out25, demultiplexer_1_out26, demultiplexer_1_out27,
       demultiplexer_1_out28, demultiplexer_1_out29, demultiplexer_1_out30, demultiplexer_1_out31;
  wire [1:0] register_1_q, register_2_q, register_3_q, register_4_q, register_5_q, register_6_q,
       register_7_q, register_8_q, register_9_q, register_10_q, register_11_q, register_12_q, register_13_q,
       register_14_q, register_15_q, register_16_q, register_17_q, register_18_q, register_19_q,
       register_20_q, register_21_q, register_22_q, register_23_q, register_24_q, register_25_q,
       register_26_q, register_27_q, register_28_q, register_29_q, register_30_q, register_31_q,
       register_32_q;

  Demultiplexer #(.enable("true"), .select(5)) demultiplexer_1 (
    .out0(demultiplexer_1_out0), .out1(demultiplexer_1_out1), .out2(demultiplexer_1_out2),
    .out3(demultiplexer_1_out3), .out4(demultiplexer_1_out4), .out5(demultiplexer_1_out5),
    .out6(demultiplexer_1_out6), .out7(demultiplexer_1_out7), .out8(demultiplexer_1_out8),
    .out9(demultiplexer_1_out9), .out10(demultiplexer_1_out10), .out11(demultiplexer_1_out11),
    .out12(demultiplexer_1_out12), .out13(demultiplexer_1_out13), .out14(demultiplexer_1_out14),
    .out15(demultiplexer_1_out15), .out16(demultiplexer_1_out16), .out17(demultiplexer_1_out17),
    .out18(demultiplexer_1_out18), .out19(demultiplexer_1_out19), .out20(demultiplexer_1_out20),
    .out21(demultiplexer_1_out21), .out22(demultiplexer_1_out22), .out23(demultiplexer_1_out23),
    .out24(demultiplexer_1_out24), .out25(demultiplexer_1_out25), .out26(demultiplexer_1_out26),
    .out27(demultiplexer_1_out27), .out28(demultiplexer_1_out28), .out29(demultiplexer_1_out29),
    .out30(demultiplexer_1_out30), .out31(demultiplexer_1_out31), .in(RegWrite), .sel(Write_Register));  // open: en
  Register #(.width(2)) register_1 (
    .D(Write_Data), .en(demultiplexer_1_out1), .Q(register_1_q), .clk(Clock));  // open: clr
  Register #(.width(2)) register_2 (
    .D(Write_Data), .en(demultiplexer_1_out0), .Q(register_2_q), .clk(Clock));  // open: clr
  Register #(.width(2)) register_3 (
    .D(Write_Data), .en(demultiplexer_1_out9), .Q(register_3_q), .clk(Clock));  // open: clr
  Register #(.width(2)) register_4 (
    .D(Write_Data), .en(demultiplexer_1_out8), .Q(register_4_q), .clk(Clock));  // open: clr
  Register #(.width(2)) register_5 (
    .D(Write_Data), .en(demultiplexer_1_out17), .Q(register_5_q), .clk(Clock));  // open: clr
  Register #(.width(2)) register_6 (
    .D(Write_Data), .en(demultiplexer_1_out16), .Q(register_6_q), .clk(Clock));  // open: clr
  Register #(.width(2)) register_7 (
    .D(Write_Data), .en(demultiplexer_1_out25), .Q(register_7_q), .clk(Clock));  // open: clr
  Register #(.width(2)) register_8 (
    .D(Write_Data), .en(demultiplexer_1_out24), .Q(register_8_q), .clk(Clock));  // open: clr
  Register #(.width(2)) register_9 (
    .D(Write_Data), .en(demultiplexer_1_out2), .Q(register_9_q), .clk(Clock));  // open: clr
  Register #(.width(2)) register_10 (
    .D(Write_Data), .en(demultiplexer_1_out10), .Q(register_10_q), .clk(Clock));  // open: clr
  Register #(.width(2)) register_11 (
    .D(Write_Data), .en(demultiplexer_1_out18), .Q(register_11_q), .clk(Clock));  // open: clr
  Register #(.width(2)) register_12 (
    .D(Write_Data), .en(demultiplexer_1_out26), .Q(register_12_q), .clk(Clock));  // open: clr
  Register #(.width(2)) register_13 (
    .D(Write_Data), .en(demultiplexer_1_out3), .Q(register_13_q), .clk(Clock));  // open: clr
  Register #(.width(2)) register_14 (
    .D(Write_Data), .en(demultiplexer_1_out11), .Q(register_14_q), .clk(Clock));  // open: clr
  Register #(.width(2)) register_15 (
    .D(Write_Data), .en(demultiplexer_1_out19), .Q(register_15_q), .clk(Clock));  // open: clr
  Register #(.width(2)) register_16 (
    .D(Write_Data), .en(demultiplexer_1_out27), .Q(register_16_q), .clk(Clock));  // open: clr
  Register #(.width(2)) register_17 (
    .D(Write_Data), .en(demultiplexer_1_out4), .Q(register_17_q), .clk(Clock));  // open: clr
  Register #(.width(2)) register_18 (
    .D(Write_Data), .en(demultiplexer_1_out12), .Q(register_18_q), .clk(Clock));  // open: clr
  Register #(.width(2)) register_19 (
    .D(Write_Data), .en(demultiplexer_1_out20), .Q(register_19_q), .clk(Clock));  // open: clr
  Register #(.width(2)) register_20 (
    .D(Write_Data), .en(demultiplexer_1_out28), .Q(register_20_q), .clk(Clock));  // open: clr
  Register #(.width(2)) register_21 (
    .D(Write_Data), .en(demultiplexer_1_out5), .Q(register_21_q), .clk(Clock));  // open: clr
  Register #(.width(2)) register_22 (
    .D(Write_Data), .en(demultiplexer_1_out13), .Q(register_22_q), .clk(Clock));  // open: clr
  Register #(.width(2)) register_23 (
    .D(Write_Data), .en(demultiplexer_1_out21), .Q(register_23_q), .clk(Clock));  // open: clr
  Register #(.width(2)) register_24 (
    .D(Write_Data), .en(demultiplexer_1_out29), .Q(register_24_q), .clk(Clock));  // open: clr
  Register #(.width(2)) register_25 (
    .D(Write_Data), .en(demultiplexer_1_out6), .Q(register_25_q), .clk(Clock));  // open: clr
  Register #(.width(2)) register_26 (
    .D(Write_Data), .en(demultiplexer_1_out14), .Q(register_26_q), .clk(Clock));  // open: clr
  Register #(.width(2)) register_27 (
    .D(Write_Data), .en(demultiplexer_1_out22), .Q(register_27_q), .clk(Clock));  // open: clr
  Register #(.width(2)) register_28 (
    .D(Write_Data), .en(demultiplexer_1_out30), .Q(register_28_q), .clk(Clock));  // open: clr
  Register #(.width(2)) register_29 (
    .D(Write_Data), .en(demultiplexer_1_out7), .Q(register_29_q), .clk(Clock));  // open: clr
  Register #(.width(2)) register_30 (
    .D(Write_Data), .en(demultiplexer_1_out15), .Q(register_30_q), .clk(Clock));  // open: clr
  Register #(.width(2)) register_31 (
    .D(Write_Data), .en(demultiplexer_1_out23), .Q(register_31_q), .clk(Clock));  // open: clr
  Register #(.width(2)) register_32 (
    .D(Write_Data), .en(demultiplexer_1_out31), .Q(register_32_q), .clk(Clock));  // open: clr
  Multiplexer #(.enable("true"), .select(5), .width(2)) multiplexer_1 (
    .in0(2'b00), .in1(register_1_q), .in2(register_9_q), .in3(register_13_q), .in4(register_17_q),
    .in5(register_21_q), .in6(register_25_q), .in7(register_29_q), .in8(register_4_q), .in9(register_3_q),
    .in10(register_10_q), .in11(register_14_q), .in12(register_18_q), .in13(register_22_q),
    .in14(register_26_q), .in15(register_30_q), .in16(register_6_q), .in17(register_5_q),
    .in18(register_11_q), .in19(register_15_q), .in20(register_19_q), .in21(register_23_q),
    .in22(register_27_q), .in23(register_31_q), .in24(register_8_q), .in25(register_7_q),
    .in26(register_12_q), .in27(register_16_q), .in28(register_20_q), .in29(register_24_q),
    .in30(register_28_q), .in31(register_32_q), .out(Read_Data_1), .sel(Read_Register_1));  // open: en
  Multiplexer #(.enable("true"), .select(5), .width(2)) multiplexer_2 (
    .in0(2'b00), .in1(register_1_q), .in2(register_9_q), .in3(register_13_q), .in4(register_17_q),
    .in5(register_21_q), .in6(register_25_q), .in7(register_29_q), .in8(register_4_q), .in9(register_3_q),
    .in10(register_10_q), .in11(register_14_q), .in12(register_18_q), .in13(register_22_q),
    .in14(register_26_q), .in15(register_30_q), .in16(register_6_q), .in17(register_5_q),
    .in18(register_11_q), .in19(register_15_q), .in20(register_19_q), .in21(register_23_q),
    .in22(register_27_q), .in23(register_31_q), .in24(register_8_q), .in25(register_7_q),
    .in26(register_12_q), .in27(register_16_q), .in28(register_20_q), .in29(register_24_q),
    .in30(register_28_q), .in31(register_32_q), .out(Read_Data_2), .sel(Read_Register_2));  // open: en
  Multiplexer #(.enable("true"), .select(5), .width(2)) multiplexer_3 (
    .in0(2'b00), .in1(register_1_q), .in2(register_9_q), .in3(register_13_q), .in4(register_17_q),
    .in5(register_21_q), .in6(register_25_q), .in7(register_29_q), .in8(register_4_q), .in9(register_3_q),
    .in10(register_10_q), .in11(register_14_q), .in12(register_18_q), .in13(register_22_q),
    .in14(register_26_q), .in15(register_30_q), .in16(register_6_q), .in17(register_5_q),
    .in18(register_11_q), .in19(register_15_q), .in20(register_19_q), .in21(register_23_q),
    .in22(register_27_q), .in23(register_31_q), .in24(register_8_q), .in25(register_7_q),
    .in26(register_12_q), .in27(register_16_q), .in28(register_20_q), .in29(register_24_q),
    .in30(register_28_q), .in31(register_32_q), .out(Read_Data_3), .sel(Read_Register_3));  // open: en
endmodule

module RS_Selector (
  input  Bsy_1,
  input  Bsy_2,
  input  Bsy_3,
  input  [5:0] Opcode,
  output [1:0] RS_Selector_Out
);

  wire and_1_out, and_2_out, and_3_out, not_1_out, not_2_out, not_3_out, not_4_out, not_5_out, not_6_out;

  not not_1 (not_1_out, Bsy_2);
  not not_2 (not_2_out, Bsy_3);
  not not_3 (not_3_out, Bsy_1);
  not not_4 (not_4_out, Opcode[5]);
  not not_5 (not_5_out, not_1_out);
  not not_6 (not_6_out, Opcode[5]);
  and and_1 (and_1_out, Opcode[5], not_2_out);
  and and_2 (and_2_out, not_4_out, not_3_out, not_5_out);
  and and_3 (and_3_out, not_6_out, not_1_out);
  or or_1 (RS_Selector_Out[0], and_1_out, and_2_out);
  or or_2 (RS_Selector_Out[1], and_1_out, and_3_out);
endmodule

module reserveStation (
  input  Clock,
  input  Bsy_in,
  input  Bsy_WE,
  input  [5:0] Op_in,
  input  Op_WE,
  input  [31:0] v1_in,
  input  v1_WE,
  input  [31:0] v2_in,
  input  v2_WE,
  input  [1:0] q1_in,
  input  q1_WE,
  input  [1:0] q2_in,
  input  q2_WE,
  input  [15:0] A_in,
  input  A_WE,
  input  Reset,
  input  [5:0] funct_in,
  input  funct_WE,
  input  [4:0] RegDest,
  input  RegDest_WE,
  output Bsy,
  output [5:0] Op,
  output [31:0] v_1,
  output [31:0] v_2,
  output [1:0] q_1,
  output [1:0] q_2,
  output [15:0] A,
  output [5:0] funct,
  output [4:0] Reg_D
);

  Register #(.width(1)) Busy (.D(Bsy_in), .en(Bsy_WE), .clk(Clock), .Q(Bsy), .clr(Reset));
  Register #(.width(6)) Opp (.D(Op_in), .en(Op_WE), .clk(Clock), .Q(Op), .clr(Reset));
  Register #(.width(32)) V1 (.D(v1_in), .en(v1_WE), .clk(Clock), .Q(v_1), .clr(Reset));
  Register #(.width(32)) V2 (.D(v2_in), .en(v2_WE), .clk(Clock), .Q(v_2), .clr(Reset));
  Register #(.width(2)) Q1 (.D(q1_in), .en(q1_WE), .clk(Clock), .Q(q_1), .clr(Reset));
  Register #(.width(2)) Q2 (.D(q2_in), .en(q2_WE), .clk(Clock), .Q(q_2), .clr(Reset));
  Register #(.width(16)) register_1 (.D(A_in), .en(A_WE), .clk(Clock), .Q(A), .clr(Reset));
  Register #(.width(6)) register_2 (.D(funct_in), .en(funct_WE), .clk(Clock), .Q(funct));  // open: clr
  Register #(.width(5)) register_3 (.D(RegDest), .en(RegDest_WE), .clk(Clock), .Q(Reg_D), .clr(Reset));
endmodule

module WriteBack (
  input  [31:0] Result_Data1,
  input  Fin_RS_1,
  input  [31:0] Result_Data2,
  input  Fin_RS_2,
  input  [31:0] Result_Data3,
  input  Fin_RS_3,
  input  Write_Enable,
  input  Clock,
  input  [4:0] Reg_D_RS1,
  input  [4:0] Reg_D_RS2,
  input  [4:0] Reg_D_RS3,
  input  Equal_RS1,
  input  Equal_RS2,
  input  Equal_RS3,
  output [31:0] WB_Data_Out,
  output [4:0] WB_Address_Out,
  output WB_Equal_Out,
  output WB_Dest_Enable,
  output [1:0] WB_RS_Out
);

  wire or_1_out, or_2_out;
  wire [1:0] multiplexer_1_out, multiplexer_6_out, multiplexer_7_out;
  wire [4:0] multiplexer_5_out, multiplexer_9_out;
  wire [31:0] multiplexer_4_out, multiplexer_8_out;

  Multiplexer #(.width(2)) multiplexer_1 (.in0(2'b00), .in1(2'b01), .out(multiplexer_1_out), .sel(Fin_RS_1));
  Multiplexer #(.width(32)) multiplexer_2 (.in0({32{1'b0}}), .in1(Result_Data1), .out(Result_Data2), .sel(Fin_RS_1));
  Multiplexer #(.width(5)) multiplexer_3 (.in0({5{1'b0}}), .in1(Reg_D_RS1), .out(Reg_D_RS2), .sel(Fin_RS_1));
  Multiplexer #(.width(32)) multiplexer_4 (.in0(Result_Data2), .out(multiplexer_4_out), .sel(Fin_RS_2));  // open: in1
  Multiplexer #(.width(5)) multiplexer_5 (.in0(Reg_D_RS2), .out(multiplexer_5_out), .sel(Fin_RS_2));  // open: in1
  Multiplexer #(.width(2)) multiplexer_6 (
    .in0(multiplexer_1_out), .in1(2'b10), .out(multiplexer_6_out), .sel(Fin_RS_2));
  Register #(.width(1)) register_1 (.D(or_1_out), .en(Write_Enable), .clk(Clock), .Q(WB_Equal_Out));  // open: clr
  or or_1 (or_1_out, Equal_RS1, Equal_RS2, Equal_RS3);
  Register #(.width(1)) register_2 (.D(or_2_out), .en(Write_Enable), .clk(Clock), .Q(WB_Dest_Enable));  // open: clr
  or or_2 (or_2_out, Fin_RS_1, Fin_RS_2, Fin_RS_3);
  Multiplexer #(.width(2)) multiplexer_7 (
    .in0(multiplexer_6_out), .in1(2'b11), .out(multiplexer_7_out), .sel(Fin_RS_3));
  Multiplexer #(.width(32)) multiplexer_8 (
    .in0(multiplexer_4_out), .in1(Result_Data3), .out(multiplexer_8_out), .sel(Fin_RS_3));
  Multiplexer #(.width(5)) multiplexer_9 (
    .in0(multiplexer_5_out), .in1(Reg_D_RS3), .out(multiplexer_9_out), .sel(Fin_RS_3));
  Register #(.width(32)) register_3 (
    .D(multiplexer_8_out), .en(Write_Enable), .clk(Clock), .Q(WB_Data_Out));  // open: clr
  Register #(.width(5)) register_4 (
    .D(multiplexer_9_out), .en(Write_Enable), .clk(Clock), .Q(WB_Address_Out));  // open: clr
  Register #(.width(2)) register_5 (.D(multiplexer_7_out), .en(Write_Enable), .clk(Clock), .Q(WB_RS_Out));  // open: clr
endmodule

module OperandoWriter (
  input  [1:0] Q,
  input  [1:0] WB_RS,
  input  WE,
  input  [31:0] V,
  input  [31:0] WB_Data,
  output WE_V_Out,
  output [31:0] V_Out
);

  wire and_1_out, comparator_1_eq, comparator_2_eq, not_1_out;
  wire [31:0] multiplexer_1_out;

  Comparator #(.mode("unsigned"), .width(2)) comparator_1 (.a(Q), .b(WB_RS), .eq(comparator_1_eq));  // open: gt, lt
  Comparator #(.mode("unsigned"), .width(2)) comparator_2 (.a(2'b00), .b(WB_RS), .eq(comparator_2_eq));  // open: gt, lt
  not not_1 (not_1_out, comparator_2_eq);
  and and_1 (and_1_out, comparator_1_eq, not_1_out);
  Multiplexer #(.width(32)) multiplexer_1 (.in0({32{1'b0}}), .in1(V), .out(multiplexer_1_out), .sel(WE));
  or or_1 (WE_V_Out, and_1_out, WE);
  Multiplexer #(.width(32)) multiplexer_2 (.in0(multiplexer_1_out), .in1(WB_Data), .out(V_Out), .sel(and_1_out));
endmodule
