// Logisim project UnicycleNovo5.circ as structural Verilog: 8 circuits, main circuit main
module main (
);

  wire ALUSrc, Branch, button_1_out, clock0, Clock1, clock_1_out, comparator_1_eq, Jump, MemtoReg, MemWrite,
       RegDst, RegWrite, set, Stall, uc_1_branch, ula_1_equal;
  wire [2:0] uc_ula_1_ulacode;
  wire [4:0] multiplexer_3_out;
  wire [9:0] adder_1_out, adder_2_out, multiplexer_1_out, multiplexer_2_out, register_1_q, rom_1_data;
  wire [19:0] ula_1_ula_out_2;
  wire [31:0] bit_extender_1_out, memoria_1_dataout, multiplexer_4_out, multiplexer_5_out,
       registerfile_1_read_data_1, registerfile_1_read_data_2, ula_1_ula_out;
  wire [31:10] rom_1_data_2;

  Register #(.width(10)) register_1 (
    .D(multiplexer_1_out), .en(set), .clk(clock0), .Q(register_1_q), .clr(button_1_out));
  Button button_1 (.out(button_1_out));
  Multiplexer #(.width(10)) multiplexer_1 (
    .in0(multiplexer_2_out), .in1(rom_1_data), .out(multiplexer_1_out), .sel(Jump));
  Adder #(.width(10)) adder_1 (.a(10'h1), .b(register_1_q), .out(adder_1_out));  // open: cin, cout
  ROM #(.addrWidth(10), .dataWidth(32)) rom_1 (.addr(register_1_q), .data({rom_1_data_2, rom_1_data}));
  Adder #(.width(10)) adder_2 (.a(adder_1_out), .b(rom_1_data), .out(adder_2_out));  // open: cin, cout
  Multiplexer #(.width(10)) multiplexer_2 (.in0(adder_1_out), .in1(adder_2_out), .out(multiplexer_2_out), .sel(Branch));
  Comparator #(.width(32)) comparator_1 (
    .a({rom_1_data_2, rom_1_data}), .b({32{1'b0}}), .eq(comparator_1_eq));  // open: gt, lt
  Clock clock_1 (.out(clock_1_out));
  and NOP (clock0, ~comparator_1_eq, clock_1_out);  // AND_Gate
  Multiplexer #(.width(5)) multiplexer_3 (
    .in0(rom_1_data_2[15:11]), .in1(rom_1_data_2[20:16]), .out(multiplexer_3_out), .sel(RegDst));
  not not_1 (set, Stall);
  Multiplexer #(.width(32)) multiplexer_4 (
    .in0({ula_1_ula_out[31:22], ula_1_ula_out_2, ula_1_ula_out[1:0]}), .in1(memoria_1_dataout),
    .out(multiplexer_4_out), .sel(MemtoReg));
  and and_1 (Clock1, clock0, set);
  UC uc_1 (
    .OpCode(rom_1_data_2[31:26]), .RegDst(RegDst), .Branch(uc_1_branch), .MemtoReg(MemtoReg),
    .MemWrite(MemWrite), .ALUSrc(ALUSrc), .RegWrite(RegWrite), .Jump(Jump));
  UC_ula uc_ula_1 (.funct(rom_1_data[5:0]), .OpCode(rom_1_data_2[31:26]), .ULAcode(uc_ula_1_ulacode));
  assign bit_extender_1_out = {{16{rom_1_data_2[15]}}, {rom_1_data_2[15:10], rom_1_data}};  // Bit_Extender bit_extender_1
  RegisterFile registerfile_1 (
    .Read_Register_1(rom_1_data_2[25:21]), .Read_Register_2(rom_1_data_2[20:16]),
    .Write_Data(multiplexer_4_out), .RegWrite(RegWrite), .Write_Register(multiplexer_3_out), .Clock(Clock1),
    .Read_Data_1(registerfile_1_read_data_1), .Read_Data_2(registerfile_1_read_data_2));
  Multiplexer #(.width(32)) multiplexer_5 (
    .in0(registerfile_1_read_data_2), .in1(bit_extender_1_out), .out(multiplexer_5_out), .sel(ALUSrc));
  and and_2 (Branch, uc_1_branch, ula_1_equal);
  ULA ula_1 (
    .A(registerfile_1_read_data_1), .B(multiplexer_5_out), .Op(uc_ula_1_ulacode),
    .shamt({rom_1_data_2[10], rom_1_data[9:6]}),
    .ULA_out({ula_1_ula_out[31:22], ula_1_ula_out_2, ula_1_ula_out[1:0]}), .Equal(ula_1_equal));
  memoria memoria_1 (
    .in_1(clock0), .Data_In(registerfile_1_read_data_2), .ReadEnable(MemtoReg), .WriteEnable(MemWrite),
    .Address(ula_1_ula_out_2), .Stall(Stall), .DataOut(memoria_1_dataout));

  // Notes on the sheet:
  //   contents of rom_1 (hex, n*v repeats v):
  //   24080000 24090000 240a0005 240d000a 112d0005 96080 10c5820 8d700000 25290001 8100004
endmodule

module RegisterFile (
  input  [4:0] Read_Register_1,
  input  [4:0] Read_Register_2,
  input  [31:0] Write_Data,
  input  RegWrite,
  input  [4:0] Write_Register,
  input  Clock,
  output [31:0] Read_Data_1,
  output [31:0] Read_Data_2
);

  wire demultiplexer_1_out0, demultiplexer_1_out1, demultiplexer_1_out2, demultiplexer_1_out3,
       demultiplexer_1_out4, demultiplexer_1_out5, demultiplexer_1_out6, demultiplexer_1_out7,
       demultiplexer_1_out8, demultiplexer_1_out9, demultiplexer_1_out10, demultiplexer_1_out11,
       demultiplexer_1_out12, demultiplexer_1_out13, demultiplexer_1_out14, demultiplexer_1_out15,
       demultiplexer_1_out16, demultiplexer_1_out17, demultiplexer_1_out18, demultiplexer_1_out19,
       demultiplexer_1_out20, demultiplexer_1_out21, demultiplexer_1_out22, demultiplexer_1_out23,
       demultiplexer_1_out24, demultiplexer_1_out25, demultiplexer_1_out26, demultiplexer_1_out27,
       demultiplexer_1_out28, demultiplexer_1_out29, demultiplexer_1_out30, demultiplexer_1_out31;
  wire [31:0] register_1_q, register_2_q, register_3_q, register_4_q, register_5_q, register_6_q,
       register_7_q, register_8_q, register_9_q, register_10_q, register_11_q, register_12_q, register_13_q,
       register_14_q, register_15_q, register_16_q, register_17_q, register_18_q, register_19_q,
       register_20_q, register_21_q, register_22_q, register_23_q, register_24_q, register_25_q,
       register_26_q, register_27_q, register_28_q, register_29_q, register_30_q, register_31_q,
       register_32_q;

  Demultiplexer #(.enable("true"), .select(5)) demultiplexer_1 (
    .out0(demultiplexer_1_out0), .out1(demultiplexer_1_out1), .out2(demultiplexer_1_out2),
    .out3(demultiplexer_1_out3), .out4(demultiplexer_1_out4), .out5(demultiplexer_1_out5),
    .out6(demultiplexer_1_out6), .out7(demultiplexer_1_out7), .out8(demultiplexer_1_out8),
    .out9(demultiplexer_1_out9), .out10(demultiplexer_1_out10), .out11(demultiplexer_1_out11),
    .out12(demultiplexer_1_out12), .out13(demultiplexer_1_out13), .out14(demultiplexer_1_out14),
    .out15(demultiplexer_1_out15), .out16(demultiplexer_1_out16), .out17(demultiplexer_1_out17),
    .out18(demultiplexer_1_out18), .out19(demultiplexer_1_out19), .out20(demultiplexer_1_out20),
    .out21(demultiplexer_1_out21), .out22(demultiplexer_1_out22), .out23(demultiplexer_1_out23),
    .out24(demultiplexer_1_out24), .out25(demultiplexer_1_out25), .out26(demultiplexer_1_out26),
    .out27(demultiplexer_1_out27), .out28(demultiplexer_1_out28), .out29(demultiplexer_1_out29),
    .out30(demultiplexer_1_out30), .out31(demultiplexer_1_out31), .in(RegWrite), .sel(Write_Register));  // open: en
  Register #(.width(32)) register_1 (
    .D(Write_Data), .en(demultiplexer_1_out1), .Q(register_1_q), .clk(Clock));  // open: clr
  Register #(.width(32)) register_2 (
    .D(Write_Data), .en(demultiplexer_1_out0), .Q(register_2_q), .clk(Clock));  // open: clr
  Register #(.width(32)) register_3 (
    .D(Write_Data), .en(demultiplexer_1_out9), .Q(register_3_q), .clk(Clock));  // open: clr
  Register #(.width(32)) register_4 (
    .D(Write_Data), .en(demultiplexer_1_out8), .Q(register_4_q), .clk(Clock));  // open: clr
  Register #(.width(32)) register_5 (
    .D(Write_Data), .en(demultiplexer_1_out17), .Q(register_5_q), .clk(Clock));  // open: clr
  Register #(.width(32)) register_6 (
    .D(Write_Data), .en(demultiplexer_1_out16), .Q(register_6_q), .clk(Clock));  // open: clr
  Register #(.width(32)) register_7 (
    .D(Write_Data), .en(demultiplexer_1_out25), .Q(register_7_q), .clk(Clock));  // open: clr
  Register #(.width(32)) register_8 (
    .D(Write_Data), .en(demultiplexer_1_out24), .Q(register_8_q), .clk(Clock));  // open: clr
  Register #(.width(32)) register_9 (
    .D(Write_Data), .en(demultiplexer_1_out2), .Q(register_9_q), .clk(Clock));  // open: clr
  Register #(.width(32)) register_10 (
    .D(Write_Data), .en(demultiplexer_1_out10), .Q(register_10_q), .clk(Clock));  // open: clr
  Register #(.width(32)) register_11 (
    .D(Write_Data), .en(demultiplexer_1_out18), .Q(register_11_q), .clk(Clock));  // open: clr
  Register #(.width(32)) register_12 (
    .D(Write_Data), .en(demultiplexer_1_out26), .Q(register_12_q), .clk(Clock));  // open: clr
  Register #(.width(32)) register_13 (
    .D(Write_Data), .en(demultiplexer_1_out3), .Q(register_13_q), .clk(Clock));  // open: clr
  Register #(.width(32)) register_14 (
    .D(Write_Data), .en(demultiplexer_1_out11), .Q(register_14_q), .clk(Clock));  // open: clr
  Register #(.width(32)) register_15 (
    .D(Write_Data), .en(demultiplexer_1_out19), .Q(register_15_q), .clk(Clock));  // open: clr
  Register #(.width(32)) register_16 (
    .D(Write_Data), .en(demultiplexer_1_out27), .Q(register_16_q), .clk(Clock));  // open: clr
  Register #(.width(32)) register_17 (
    .D(Write_Data), .en(demultiplexer_1_out4), .Q(register_17_q), .clk(Clock));  // open: clr
  Register #(.width(32)) register_18 (
    .D(Write_Data), .en(demultiplexer_1_out12), .Q(register_18_q), .clk(Clock));  // open: clr
  Register #(.width(32)) register_19 (
    .D(Write_Data), .en(demultiplexer_1_out20), .Q(register_19_q), .clk(Clock));  // open: clr
  Register #(.width(32)) register_20 (
    .D(Write_Data), .en(demultiplexer_1_out28), .Q(register_20_q), .clk(Clock));  // open: clr
  Register #(.width(32)) register_21 (
    .D(Write_Data), .en(demultiplexer_1_out5), .Q(register_21_q), .clk(Clock));  // open: clr
  Register #(.width(32)) register_22 (
    .D(Write_Data), .en(demultiplexer_1_out13), .Q(register_22_q), .clk(Clock));  // open: clr
  Register #(.width(32)) register_23 (
    .D(Write_Data), .en(demultiplexer_1_out21), .Q(register_23_q), .clk(Clock));  // open: clr
  Register #(.width(32)) register_24 (
    .D(Write_Data), .en(demultiplexer_1_out29), .Q(register_24_q), .clk(Clock));  // open: clr
  Register #(.width(32)) register_25 (
    .D(Write_Data), .en(demultiplexer_1_out6), .Q(register_25_q), .clk(Clock));  // open: clr
  Register #(.width(32)) register_26 (
    .D(Write_Data), .en(demultiplexer_1_out14), .Q(register_26_q), .clk(Clock));  // open: clr
  Register #(.width(32)) register_27 (
    .D(Write_Data), .en(demultiplexer_1_out22), .Q(register_27_q), .clk(Clock));  // open: clr
  Register #(.width(32)) register_28 (
    .D(Write_Data), .en(demultiplexer_1_out30), .Q(register_28_q), .clk(Clock));  // open: clr
  Register #(.width(32)) register_29 (
    .D(Write_Data), .en(demultiplexer_1_out7), .Q(register_29_q), .clk(Clock));  // open: clr
  Register #(.width(32)) register_30 (
    .D(Write_Data), .en(demultiplexer_1_out15), .Q(register_30_q), .clk(Clock));  // open: clr
  Register #(.width(32)) register_31 (
    .D(Write_Data), .en(demultiplexer_1_out23), .Q(register_31_q), .clk(Clock));  // open: clr
  Register #(.width(32)) register_32 (
    .D(Write_Data), .en(demultiplexer_1_out31), .Q(register_32_q), .clk(Clock));  // open: clr
  Multiplexer #(.enable("true"), .select(5), .width(32)) multiplexer_1 (
    .in0({32{1'b0}}), .in1(register_1_q), .in2(register_9_q), .in3(register_13_q), .in4(register_17_q),
    .in5(register_21_q), .in6(register_25_q), .in7(register_29_q), .in8(register_4_q), .in9(register_3_q),
    .in10(register_10_q), .in11(register_14_q), .in12(register_18_q), .in13(register_22_q),
    .in14(register_26_q), .in15(register_30_q), .in16(register_6_q), .in17(register_5_q),
    .in18(register_11_q), .in19(register_15_q), .in20(register_19_q), .in21(register_23_q),
    .in22(register_27_q), .in23(register_31_q), .in24(register_8_q), .in25(register_7_q),
    .in26(register_12_q), .in27(register_16_q), .in28(register_20_q), .in29(register_24_q),
    .in30(register_28_q), .in31(register_32_q), .out(Read_Data_1), .sel(Read_Register_1));  // open: en
  Multiplexer #(.enable("true"), .select(5), .width(32)) multiplexer_2 (
    .in0({32{1'b0}}), .in1(register_1_q), .in2(register_9_q), .in3(register_13_q), .in4(register_17_q),
    .in5(register_21_q), .in6(register_25_q), .in7(register_29_q), .in8(register_4_q), .in9(register_3_q),
    .in10(register_10_q), .in11(register_14_q), .in12(register_18_q), .in13(register_22_q),
    .in14(register_26_q), .in15(register_30_q), .in16(register_6_q), .in17(register_5_q),
    .in18(register_11_q), .in19(register_15_q), .in20(register_19_q), .in21(register_23_q),
    .in22(register_27_q), .in23(register_31_q), .in24(register_8_q), .in25(register_7_q),
    .in26(register_12_q), .in27(register_16_q), .in28(register_20_q), .in29(register_24_q),
    .in30(register_28_q), .in31(register_32_q), .out(Read_Data_2), .sel(Read_Register_2));  // open: en
endmodule

module ULA (
  input  [31:0] A,
  input  [31:0] B,
  input  [2:0] Op,
  input  [4:0] shamt,
  output [31:0] ULA_out,
  output Equal
);

  wire comparator_1_lt;
  wire [31:0] adder_1_out, multiplexer_1_out, nor_1_out, shifter_1_out, subtractor_1_out;

  Adder #(.width(32)) adder_1 (.a(A), .b(B), .out(adder_1_out));  // open: cin, cout
  Subtractor #(.width(32)) subtractor_1 (.a(A), .b(B), .out(subtractor_1_out));  // open: bin, bout
  assign nor_1_out = ~(A | B);  // NOR_Gate nor_1, 32 bits wide
  Comparator #(.width(32)) comparator_1 (.a(A), .b(B), .eq(Equal), .lt(comparator_1_lt));  // open: gt
  Multiplexer #(.width(32)) multiplexer_1 (
    .in0({32{1'b0}}), .in1(32'h1), .out(multiplexer_1_out), .sel(comparator_1_lt));
  Shifter #(.width(32)) shifter_1 (.in(B), .\dist (shamt), .out(shifter_1_out));
  Multiplexer #(.select(3), .width(32)) multiplexer_2 (
    .in0(subtractor_1_out), .in1(nor_1_out), .in2(multiplexer_1_out), .in3(shifter_1_out), .in4(adder_1_out),
    .in5(adder_1_out), .in6(adder_1_out), .in7(adder_1_out), .out(ULA_out), .sel(Op));
endmodule

module UC (
  input  [5:0] OpCode,
  output RegDst,
  output Branch,
  output MemtoReg,
  output MemWrite,
  output ALUSrc,
  output RegWrite,
  output Jump
);

  wire ADDIU_out, Tipo_R_out;

  and J (Jump, ~OpCode[5], ~OpCode[4], ~OpCode[3], ~OpCode[2], OpCode[1], ~OpCode[0]);  // AND_Gate
  and BEQ (Branch, ~OpCode[5], ~OpCode[4], ~OpCode[3], OpCode[2], ~OpCode[1], ~OpCode[0]);  // AND_Gate
  and SW (MemWrite, OpCode[5], ~OpCode[4], OpCode[3], ~OpCode[2], OpCode[1], OpCode[0]);  // AND_Gate
  and LW (MemtoReg, OpCode[5], ~OpCode[4], ~OpCode[3], ~OpCode[2], OpCode[1], OpCode[0]);  // AND_Gate
  and ADDIU (ADDIU_out, ~OpCode[5], ~OpCode[4], OpCode[3], ~OpCode[2], ~OpCode[1], OpCode[0]);  // AND_Gate
  and Tipo_R (Tipo_R_out, ~OpCode[5], ~OpCode[4], ~OpCode[3], ~OpCode[2], ~OpCode[1], ~OpCode[0]);  // AND_Gate
  or or_1 (RegDst, ADDIU_out, MemtoReg);
  or or_2 (ALUSrc, ADDIU_out, MemtoReg, MemWrite);
  or or_3 (RegWrite, Tipo_R_out, ADDIU_out, MemtoReg);
endmodule

module UC_ula (
  input  [5:0] funct,
  input  [5:0] OpCode,
  output [2:0] ULAcode
);

  wire NOR0_out, nor_1_out, not_R_out, SLL0_out, SLT0_out, SUB0_out;

  and SLL0 (SLL0_out, ~funct[5], ~funct[4], ~funct[3], ~funct[2], ~funct[1], ~funct[0]);  // AND_Gate
  and SLT0 (SLT0_out, funct[5], ~funct[4], funct[3], ~funct[2], funct[1], ~funct[0]);  // AND_Gate
  and NOR0 (NOR0_out, funct[5], ~funct[4], ~funct[3], funct[2], funct[1], funct[0]);  // AND_Gate
  nand not_R (not_R_out, ~OpCode[0], ~OpCode[1], ~OpCode[2], ~OpCode[3], ~OpCode[4], ~OpCode[5]);  // NAND_Gate
  and SUB0 (SUB0_out, funct[5], ~funct[4], ~funct[3], ~funct[2], funct[1], ~funct[0]);  // AND_Gate
  or or_1 (ULAcode[0], NOR0_out, SLL0_out);
  or or_2 (ULAcode[1], SLT0_out, SLL0_out);
  nor nor_1 (nor_1_out, SUB0_out, NOR0_out, SLT0_out, SLL0_out);
  or or_3 (ULAcode[2], nor_1_out, not_R_out);
endmodule

module memoria (
  input  in_1,
  input  [31:0] Data_In,
  input  ReadEnable,
  input  WriteEnable,
  input  [19:0] Address,
  output Stall,
  output [31:0] DataOut
);

  wire and_1_out, and_2_out, and_3_out, and_4_out, cache_1_hit, ClockofRAM, demultiplexer_1_out0,
       demultiplexer_1_out1, demultiplexer_1_out2, demultiplexer_1_out3, Miss, not_1_out, not_2_out,
       or_1_out, register_1_q, S1, S2, t_ff_1_q;
  wire [31:0] ram_1_dout, ram_2_dout, ram_3_dout, ram_4_dout;

  clockRAM clockram_1 (.ClockIN(in_1), .ClockOut(ClockofRAM));
  Demultiplexer #(.select(2)) demultiplexer_1 (
    .out0(demultiplexer_1_out0), .out1(demultiplexer_1_out1), .out2(demultiplexer_1_out2),
    .out3(demultiplexer_1_out3), .in(WriteEnable), .sel(Address[1:0]));
  RAM #(.addrWidth(18), .dataWidth(32), .enables("line")) ram_1 (
    .addr(Address[19:2]), .we(demultiplexer_1_out0), .clk(ClockofRAM), .din(Data_In), .dout(ram_1_dout));
  RAM #(.addrWidth(18), .dataWidth(32), .enables("line")) ram_2 (
    .addr(Address[19:2]), .we(demultiplexer_1_out1), .clk(ClockofRAM), .din(Data_In), .dout(ram_2_dout));
  RAM #(.addrWidth(18), .dataWidth(32), .enables("line")) ram_3 (
    .addr(Address[19:2]), .we(demultiplexer_1_out2), .clk(ClockofRAM), .din(Data_In), .dout(ram_3_dout));
  RAM #(.addrWidth(18), .dataWidth(32), .enables("line")) ram_4 (
    .addr(Address[19:2]), .we(demultiplexer_1_out3), .clk(ClockofRAM), .din(Data_In), .dout(ram_4_dout));
  and and_1 (and_1_out, ReadEnable, Miss);
  or or_1 (or_1_out, WriteEnable, and_1_out);
  not not_1 (not_1_out, S2);
  not not_2 (not_2_out, S1);
  T_Flip_Flop t_ff_1 (.T(or_1_out), .clk(in_1), .Q(t_ff_1_q), .reset(register_1_q));  // open: Qn, preset
  and and_2 (and_2_out, WriteEnable, not_1_out);
  and and_3 (and_3_out, and_1_out, not_2_out);
  and and_4 (and_4_out, WriteEnable, t_ff_1_q);
  T_Flip_Flop t_ff_2 (.T(and_4_out), .clk(in_1), .Q(S1), .reset(register_1_q));  // open: Qn, preset
  and and_5 (S2, t_ff_1_q, S1);
  Register #(.width(1)) register_1 (.D(S2), .en(in_1), .clk(in_1), .Q(register_1_q));  // open: clr
  or or_2 (Stall, and_2_out, and_3_out);
  not not_3 (Miss, cache_1_hit);
  Cache cache_1 (
    .MemIn1(ram_1_dout), .MemIn2(ram_2_dout), .MemIn3(ram_3_dout), .MemIn4(ram_4_dout), .Clock(in_1),
    .ReadEnable(ReadEnable), .WriteEnable(WriteEnable), .Address(Address), .Hit(cache_1_hit),
    .DataOut(DataOut));

  // Other names for the same wires on the sheet: AdrMem[17:0] = Address[19:2]; Clock = in_1; RE = ReadEnable;
  //   WE = WriteEnable
endmodule

module clockRAM (
  input  ClockIN,
  output ClockOut
);

  wire button_1_out;

  Button button_1 (.out(button_1_out));
  T_Flip_Flop t_ff_1 (.T(ClockIN), .clk(ClockIN), .Q(ClockOut), .reset(button_1_out));  // open: Qn, preset
endmodule

module Cache (
  input  [31:0] MemIn1,
  input  [31:0] MemIn2,
  input  [31:0] MemIn3,
  input  [31:0] MemIn4,
  input  Clock,
  input  ReadEnable,
  input  WriteEnable,
  input  [19:0] Address,
  output Hit,
  output [31:0] DataOut
);

  wire and_1_out, and_2_out, comparator_1_eq, d_ff_1_q, not_1_out, register_3_q, t_ff_1_q, t_ff_2_q, WE;
  wire [15:0] bit_extender_1_out, register_1_q, register_2_q, tag_dout;
  wire [31:0] Out1, Out2, Out3, Out4;

  not not_1 (not_1_out, Hit);
  D_Flip_Flop d_ff_1 (.D(not_1_out), .clk(Clock), .Q(d_ff_1_q));  // open: Qn, preset, reset
  or or_1 (WE, d_ff_1_q, WriteEnable);
  RAM #(.addrWidth(3), .dataWidth(32)) RAMCache1 (
    .addr(Address[4:2]), .we(WE), .oe(ReadEnable), .clk(Clock), .din(MemIn1), .dout(Out1));
  assign bit_extender_1_out = {{1{1'b1}}, Address[19:5]};  // Bit_Extender bit_extender_1
  Register #(.width(16)) register_1 (.D(bit_extender_1_out), .en(WE), .clk(Clock), .Q(register_1_q), .clr(and_2_out));
  T_Flip_Flop t_ff_1 (.T(WE), .clk(Clock), .Q(t_ff_1_q), .reset(and_2_out));  // open: Qn, preset
  Register #(.width(16)) register_2 (.D(register_1_q), .en(WE), .clk(t_ff_1_q), .Q(register_2_q), .clr(and_2_out));
  T_Flip_Flop t_ff_2 (.T(t_ff_1_q), .clk(Clock), .Q(t_ff_2_q), .reset(and_2_out));  // open: Qn, preset
  Register #(.width(1)) register_3 (.D(and_1_out), .en(Clock), .clk(Clock), .Q(register_3_q), .clr(and_2_out));
  and and_1 (and_1_out, t_ff_1_q, t_ff_2_q);
  RAM #(.addrWidth(3), .dataWidth(32)) RAMCache2 (
    .addr(Address[4:2]), .we(WE), .oe(ReadEnable), .clk(Clock), .din(MemIn2), .dout(Out2));
  and and_2 (and_2_out, register_3_q, t_ff_1_q);
  RAM #(.addrWidth(3), .dataWidth(16), .enables("line")) tag (
    .addr(Address[4:2]), .we(WE), .clk(Clock), .din(register_2_q), .dout(tag_dout));
  RAM #(.addrWidth(3), .dataWidth(32)) RAMCache3 (
    .addr(Address[4:2]), .we(WE), .oe(ReadEnable), .clk(Clock), .din(MemIn3), .dout(Out3));
  Comparator #(.width(15)) comparator_1 (.a(Address[19:5]), .b(tag_dout[14:0]), .eq(comparator_1_eq));  // open: gt, lt
  and and_3 (Hit, comparator_1_eq, tag_dout[15]);
  Multiplexer #(.select(2), .width(32)) multiplexer_1 (
    .in0(Out1), .in1(Out2), .in2(Out3), .in3(Out4), .out(DataOut), .sel(Address[1:0]));
  RAM #(.addrWidth(3), .dataWidth(32)) RAMCache4 (
    .addr(Address[4:2]), .we(WE), .oe(ReadEnable), .clk(Clock), .din(MemIn4), .dout(Out4));

  // Other names for the same wires on the sheet: Ad[19:0] = Address; Offset[1:0] = Address[1:0];
  //   Line[2:0] = Address[4:2]; Tag[14:0] = Address[19:5]; MI1[31:0] = MemIn1; MI2[31:0] = MemIn2; MI3[31:0] = MemIn3;
  //   MI4[31:0] = MemIn4; RE = ReadEnable
endmodule
